// Logisim project Not_And_XOR_Gate.circ as structural Verilog: 1 circuit, main circuit main
module main (
  input  And_Gate,
  input  in_2,
  input  Or_Gate,
  input  in_4,
  input  in_5,
  input  in_6,
  input  in_7,
  input  in_8,
  input  in_9,
  input  in_10,
  output out_11,
  output out_12,
  output out_13,
  output out_14,
  output out_15,
  output out_16
);

  wire pull_resistor_4_node, transistor_1_out, transistor_3_out, transistor_12_out, transistor_14_out;

  Transistor #(.\type ("n")) transistor_1 (.in(1'b1), .out(transistor_1_out), .gate(in_8));
  Pull_Resistor pull_resistor_1 (.node(transistor_1_out));
  Pull_Resistor pull_resistor_2 (.node(out_11));
  Transistor #(.\type ("n")) transistor_2 (.in(transistor_3_out), .out(out_11), .gate(And_Gate));
  Transistor #(.\type ("n")) transistor_3 (.in(1'b1), .out(transistor_3_out), .gate(in_4));
  Transistor #(.gate("br")) transistor_4 (.in(transistor_1_out), .out(out_14), .gate(in_9));
  Pull_Resistor pull_resistor_3 (.node(out_14));
  Transistor transistor_5 (.in(pull_resistor_4_node), .out(out_14), .gate(transistor_1_out));
  Pull_Resistor pull_resistor_4 (.node(pull_resistor_4_node));
  Transistor #(.\type ("n")) transistor_6 (.in(1'b1), .out(pull_resistor_4_node), .gate(in_9));
  Transistor #(.\type ("n")) transistor_7 (.in(1'b1), .out(out_13), .gate(in_2));
  Transistor transistor_8 (.in(1'b1), .out(out_16), .gate(in_10));
  Transistor #(.\type ("n")) transistor_9 (.in(1'b1), .out(out_13), .gate(Or_Gate));
  Pull_Resistor pull_resistor_5 (.node(out_15));
  Transistor transistor_10 (.in(1'b1), .out(out_15), .gate(in_7));
  Transistor #(.\type ("n")) transistor_11 (.in(1'b0), .out(out_16), .gate(in_10));
  Pull_Resistor pull_resistor_6 (.node(out_13));
  Transistor transistor_12 (.in(1'b1), .out(transistor_12_out), .gate(in_5));
  Transistor transistor_13 (.in(1'b1), .out(transistor_12_out), .gate(in_6));
  Transistor transistor_14 (.in(transistor_12_out), .out(transistor_14_out), .gate(in_5));
  Transistor transistor_15 (.in(transistor_14_out), .out(out_12), .gate(in_6));
  Pull_Resistor pull_resistor_7 (.node(out_12));

  // Notes on the sheet:
  //   XOr Gate
  //   Not Gate
  //   Not Gate
  //   NOR Gate
endmodule
