// Logisim project OR Gate for numbers.circ as structural Verilog: 1 circuit, main circuit main
module main (
);

  wire button_1_out, button_2_out, button_3_out, button_4_out, button_5_out, button_6_out, button_7_out,
       button_8_out, button_9_out, button_10_out, or_1_out, or_2_out, or_3_out;

  Button button_1 (.out(button_1_out));
  Button button_2 (.out(button_2_out));
  Button button_3 (.out(button_3_out));
  Button button_4 (.out(button_4_out));
  Button button_5 (.out(button_5_out));
  Button button_6 (.out(button_6_out));
  Button button_7 (.out(button_7_out));
  Button button_8 (.out(button_8_out));
  Button button_9 (.out(button_9_out));
  Button button_10 (.out(button_10_out));
  or or_1 (or_1_out, button_2_out, button_10_out, button_8_out, button_1_out, button_3_out, button_6_out, button_5_out, button_9_out);
  or or_2 (or_2_out, button_2_out, button_1_out, button_4_out, button_7_out, button_9_out, button_8_out, button_10_out);
  or or_3 (or_3_out, button_1_out, button_4_out, button_3_out, button_7_out, button_6_out, button_5_out, button_9_out, button_8_out, button_10_out);
  _7_Segment_Display u_7_segment_display_1 (.a(or_1_out), .b(or_2_out), .c(or_3_out));  // open: g, f, e, d, dp

  // Notes on the sheet:
  //   0: 1,2,3,5,6,7 (4,8)
  //   1: 3,6
  //   2: 1,3,4, 5,7
  //   3: 1,3,4,6,7
  //   4: 2,3,4,6
  //   5: 1,2, 4, 6, 7
  //   6: 1,2,4,5,6,7
  //   7: 1,3,6
  //   8: 1,2,3,4,5,6,7
  //   9: 1,2,3,4,6,7
endmodule
