// Logisim project l1_and_2.circ as structural Verilog: 1 circuit, main circuit main
module main (
);

  wire button_1_out, button_2_out, or_1_out, or_2_out;

  Button button_1 (.out(button_1_out));
  Button button_2 (.out(button_2_out));
  or or_1 (or_1_out, button_2_out, button_1_out);
  Button button_3 ();  // open: out
  Button button_4 ();  // open: out
  Button button_5 ();  // open: out
  _7_Segment_Display u_7_segment_display_1 (
    .f(button_2_out), .a(button_2_out), .b(or_2_out), .e(button_2_out), .d(button_2_out), .c(or_1_out));  // open: g, dp
  Button button_6 ();  // open: out
  Button button_7 ();  // open: out
  Button button_8 ();  // open: out
  Button button_9 ();  // open: out
  Button button_10 ();  // open: out
  or or_2 (or_2_out, button_2_out, button_1_out);
endmodule
